# Fritzing sketch A_type_sensor_node (saved by Fritzing 0.9.2b)
breadboards: 1

parts:
  Part1 = Arduino Pro Mini v13
  DHT1 = DHT22 Humidity and Temperature Sensor
  IC1 = ADS1115 16-bit ADC Breakout
  Part2 = OpenLog
  U1 = AVR 10-pin ICSP Header [package=2x5-shrouded_smd]
  R1 = Resistor [tolerance=±5% resistance=10k package=THT]
  C2 = Ceramic Capacitor [capacitance=100nF package="100 mil [THT, multilayer]"]
  C6 = Ceramic Capacitor [capacitance=10nF package="100 mil [THT, multilayer]"]
  Power_plug1 = Power plug

nets:
  N1: Part1.A4, IC1.SDA
  N2: Part1.A5, IC1.SCL
  GND: Part1.GND, Part1.RESET, DHT1.GND, IC1.GND, IC1.ADDR, Part2.GND, U1.2, C2.1, C6.0, Power_plug1.GND
  VCC: Part1.VCC, Part1.A3, Part1.D13/SCK, DHT1.VDD, IC1.VDD, Part2.VCC, U1.1, R1.Pin_0, C2.0, C6.1, Power_plug1.VCC
  N3: Part1.A0, U1.9
  N4: Part1.D10_PWM/SS, DHT1.DATA, R1.Pin_1
  N5: Part1.D9_PWM, Part2.RXI
  N6: IC1.A0, U1.6
  N7: IC1.A1, U1.5
  N8: IC1.A2, U1.8
  N9: IC1.A3, U1.7

custom parts:
  ADS1115 16-bit ADC Breakout: ADS1015 12-bit I2C ADC+PGA Breakout
